// Digital circuit divider.dig as structural Verilog
module divider (
  input  clk_i,
  input  reset_i,
  input  [3:0] dividend_i,
  input  [3:0] divisor_i,
  input  start_i,
  output busy_o,
  output finish_o,
  output [4:0] quotient_o
);

  divider_inside divider_inside_1 (
    .dividend_i(dividend_i), .divisor_i(divisor_i), .start_i(start_i), .clk_i(clk_i), .reset_i(reset_i),
    .busy_o(busy_o), .finish_o(finish_o), .quotient_o(quotient_o));
endmodule
