// Digital circuit nextstatelogic_gates.dig as structural Verilog
module nextstatelogic_gates (
  input  state_now_1,
  input  state_now_0,
  input  start_i,
  input  divisor__eq_0,
  input  subtrahend_gt__eq_divisor,
  output state_next_1,
  output state_next_0
);

  wire nand_1_out, nand_2_out, nand_3_out, nand_4_out, not_1_out, not_2_out, not_3_out, not_4_out;

  not not_1 (not_1_out, state_now_1);
  not not_2 (not_2_out, state_now_0);
  not not_3 (not_3_out, divisor__eq_0);
  not not_4 (not_4_out, subtrahend_gt__eq_divisor);
  nand nand_1 (nand_1_out, not_3_out, start_i, not_1_out);
  nand nand_2 (nand_2_out, state_now_0, not_4_out);
  nand nand_3 (nand_3_out, divisor__eq_0, start_i, not_2_out, not_1_out);
  nand nand_4 (nand_4_out, state_now_0, subtrahend_gt__eq_divisor);
  nand nand_5 (state_next_1, nand_1_out, nand_2_out);
  nand nand_6 (state_next_0, nand_3_out, nand_4_out);
endmodule
