// Digital circuit divider_inside.dig as structural Verilog
module divider_inside (
  input  [3:0] dividend_i,
  input  [3:0] divisor_i,
  input  start_i,
  input  clk_i,
  input  reset_i,
  output busy_o,
  output finish_o,
  output [4:0] quotient_o
);

  wire comparator_1_eq, comparator_1_gt, comparator_1_lt, comparator_2_eq, comparator_2_gt, or_1_out,
       or_2_out;
  wire [1:0] statemachine_1_state;
  wire [3:0] multiplexer_1_out, sub_1_s, subtrahend_q;
  wire [4:0] add_1_s, multiplexer_4_out, multiplexer_5_out, multiplexer_6_out, multiplexer_7_out;

  Comparator #(.Bits(4)) comparator_1 (
    .a(divisor_i), .b(4'b0000), .gt(comparator_1_gt), .eq(comparator_1_eq), .lt(comparator_1_lt));
  Comparator #(.Bits(4)) comparator_2 (
    .a(subtrahend_q), .b(divisor_i), .gt(comparator_2_gt), .eq(comparator_2_eq));  // open: lt
  or or_1 (or_1_out, comparator_1_gt, comparator_1_lt);
  or or_2 (or_2_out, comparator_2_gt, comparator_2_eq);
  statemachine statemachine_1 (
    .start_i(start_i), .divisor__eq_0(or_1_out), .substrahend_gt__eq_divisor(or_2_out), .clk(clk_i),
    .reset_i(reset_i), .state(statemachine_1_state));
  Sub #(.Bits(4)) sub_1 (.a(subtrahend_q), .b(divisor_i), .c_i(1'b0), .s(sub_1_s));  // open: c_o
  Multiplexer #(.Selector_Bits(2), .Bits(4)) multiplexer_1 (
    .sel(statemachine_1_state), .in_0(dividend_i), .in_1(sub_1_s), .in_2(subtrahend_q), .in_3(4'b0000),
    .out(multiplexer_1_out));
  Multiplexer #(.Selector_Bits(2)) multiplexer_2 (
    .sel(statemachine_1_state), .in_0(1'b0), .in_1(1'b1), .in_2(1'b0), .in_3(1'b0), .out(busy_o));
  Multiplexer #(.Selector_Bits(2)) multiplexer_3 (
    .sel(statemachine_1_state), .in_0(1'b0), .in_1(1'b0), .in_2(1'b1), .in_3(1'b0), .out(finish_o));
  Multiplexer #(.Bits(5)) multiplexer_4 (
    .sel(comparator_1_eq), .in_0(quotient_o), .in_1({5{1'b1}}), .out(multiplexer_4_out));
  D_FF_AS #(.Bits(4)) subtrahend (
    .Set(1'b0), .D(multiplexer_1_out), .C(clk_i), .Clr(reset_i), .Q(subtrahend_q));  // open: nQ
  Multiplexer #(.Bits(5)) multiplexer_5 (
    .sel(comparator_1_eq), .in_0({5{1'b0}}), .in_1(multiplexer_4_out), .out(multiplexer_5_out));
  Multiplexer #(.Selector_Bits(2), .Bits(5)) multiplexer_6 (
    .sel(statemachine_1_state), .in_0(multiplexer_5_out), .in_1(add_1_s), .in_2(multiplexer_4_out),
    .in_3({5{1'b0}}), .out(multiplexer_6_out));
  Add #(.Bits(5)) add_1 (.a(quotient_o), .b(multiplexer_7_out), .c_i(1'b0), .s(add_1_s));  // open: c_o
  Multiplexer #(.Bits(5)) multiplexer_7 (.sel(or_2_out), .in_0({5{1'b0}}), .in_1(5'b00001), .out(multiplexer_7_out));
  D_FF_AS #(.Bits(5)) quotient (
    .Set(1'b0), .D(multiplexer_6_out), .C(clk_i), .Clr(reset_i), .Q(quotient_o));  // open: nQ
endmodule
