// Digital circuit statemachine.dig as structural Verilog
module statemachine (
  input  start_i,
  input  divisor__eq_0,
  input  substrahend_gt__eq_divisor,
  input  clk,
  input  reset_i,
  output [1:0] state
);

  wire [1:0] nextstatelogic_gates_1_state_next_1;

  nextstatelogic_gates nextstatelogic_gates_1 (
    .state_now_1(state[1]), .state_now_0(state[0]), .start_i(start_i), .divisor__eq_0(divisor__eq_0),
    .subtrahend_gt__eq_divisor(substrahend_gt__eq_divisor),
    .state_next_1(nextstatelogic_gates_1_state_next_1[1]),
    .state_next_0(nextstatelogic_gates_1_state_next_1[0]));
  D_FF_AS #(.Bits(2)) d_ff_as_1 (
    .Set(1'b0), .D(nextstatelogic_gates_1_state_next_1), .C(clk), .Clr(reset_i), .Q(state));  // open: nQ
endmodule
